// Logisim project ASYNCHRONOUS_DOWN.circ as structural Verilog: 1 circuit, main circuit main
module main (
  input  in_1,
  output out_2,
  output out_3,
  output out_4
);

  wire clock_1_out;

  Clock clock_1 (.out(clock_1_out));
  T_Flip_Flop t_ff_1 (.T(in_1), .clk(clock_1_out), .Q(out_4));  // open: Qn, reset, preset
  T_Flip_Flop t_ff_2 (.T(in_1), .clk(out_4), .Q(out_3));  // open: Qn, reset, preset
  T_Flip_Flop t_ff_3 (.T(in_1), .clk(out_3), .Q(out_2));  // open: Qn, reset, preset

  // Notes on the sheet:
  //   ASYNCHRONOUS DOWN
  //   C
  //   B
  //   A
endmodule
