// Logisim project ASYNCHRONOUS_UP_COUNTER.circ as structural Verilog: 1 circuit, main circuit main
module main (
  input  in_1,
  output out_2,
  output out_3,
  output out_4
);

  wire clock_1_out, t_ff_1_qn, t_ff_2_qn;

  Clock clock_1 (.out(clock_1_out));
  T_Flip_Flop t_ff_1 (.T(in_1), .clk(clock_1_out), .Q(out_4), .Qn(t_ff_1_qn));  // open: reset, preset
  T_Flip_Flop t_ff_2 (.T(in_1), .clk(t_ff_1_qn), .Q(out_3), .Qn(t_ff_2_qn));  // open: reset, preset
  T_Flip_Flop t_ff_3 (.T(in_1), .clk(t_ff_2_qn), .Q(out_2));  // open: Qn, reset, preset

  // Notes on the sheet:
  //   ASYNCHRONOUD UP COUNTER
endmodule
