// Logisim project BASIC_REGISTER.circ as structural Verilog: 1 circuit, main circuit main
module main (
  input  in_1,
  input  in_2,
  input  in_3,
  input  in_4,
  output out_5,
  output out_6,
  output out_7,
  output out_8
);

  wire clock_1_out;

  Clock clock_1 (.out(clock_1_out));
  D_Flip_Flop d_ff_1 (.D(in_1), .clk(clock_1_out), .Q(out_5));  // open: Qn, preset, reset
  D_Flip_Flop d_ff_2 (.D(in_2), .clk(clock_1_out), .Q(out_6));  // open: Qn, preset, reset
  D_Flip_Flop d_ff_3 (.D(in_3), .clk(clock_1_out), .Q(out_7));  // open: Qn, preset, reset
  D_Flip_Flop d_ff_4 (.D(in_4), .clk(clock_1_out), .Q(out_8));  // open: Qn, preset, reset

  // Notes on the sheet:
  //   A BASIC REGISTER
endmodule
