// Logisim project PIPO_PISO.circ as structural Verilog: 1 circuit, main circuit main
module main (
  input  SERIAL_INPUT,
  input  LOAD_SHIFT,
  input  in_3,
  input  in_4,
  input  in_5,
  input  in_6,
  output SERIAL_OUTPUT
);

  wire clock_1_out, d_ff_1_q, d_ff_2_q, d_ff_3_q, multiplexer_1_out, multiplexer_2_out, multiplexer_3_out,
       multiplexer_4_out;

  D_Flip_Flop d_ff_1 (.D(multiplexer_1_out), .clk(clock_1_out), .Q(d_ff_1_q));  // open: Qn, preset, reset
  Multiplexer multiplexer_1 (.in0(SERIAL_INPUT), .in1(in_3), .out(multiplexer_1_out), .sel(LOAD_SHIFT));
  Clock clock_1 (.out(clock_1_out));
  LED led_1 (.in(d_ff_1_q));
  Multiplexer multiplexer_2 (.in0(d_ff_1_q), .in1(in_4), .out(multiplexer_2_out), .sel(LOAD_SHIFT));
  D_Flip_Flop d_ff_2 (.D(multiplexer_2_out), .clk(clock_1_out), .Q(d_ff_2_q));  // open: Qn, preset, reset
  LED led_2 (.in(d_ff_2_q));
  Multiplexer multiplexer_3 (.in0(d_ff_2_q), .in1(in_5), .out(multiplexer_3_out), .sel(LOAD_SHIFT));
  D_Flip_Flop d_ff_3 (.D(multiplexer_3_out), .clk(clock_1_out), .Q(d_ff_3_q));  // open: Qn, preset, reset
  LED led_3 (.in(d_ff_3_q));
  Multiplexer multiplexer_4 (.in0(d_ff_3_q), .in1(in_6), .out(multiplexer_4_out), .sel(LOAD_SHIFT));
  LED led_4 (.in(SERIAL_OUTPUT));
  D_Flip_Flop d_ff_4 (.D(multiplexer_4_out), .clk(clock_1_out), .Q(SERIAL_OUTPUT));  // open: Qn, preset, reset

  // Notes on the sheet:
  //   PIPO AND PISO
  //   0- LOAD
  //   1- SHIFT
endmodule
