// Logisim project SIPO_REGISTER.circ as structural Verilog: 1 circuit, main circuit main
module main (
  input  in_1
);

  wire clock_1_out, d_ff_1_q, d_ff_2_q, d_ff_3_q, d_ff_4_q;

  D_Flip_Flop d_ff_1 (.D(in_1), .clk(clock_1_out), .Q(d_ff_1_q));  // open: Qn, preset, reset
  Clock clock_1 (.out(clock_1_out));
  LED led_1 (.in(d_ff_1_q));
  D_Flip_Flop d_ff_2 (.D(d_ff_1_q), .clk(clock_1_out), .Q(d_ff_2_q));  // open: Qn, preset, reset
  LED led_2 (.in(d_ff_2_q));
  D_Flip_Flop d_ff_3 (.D(d_ff_2_q), .clk(clock_1_out), .Q(d_ff_3_q));  // open: Qn, preset, reset
  LED led_3 (.in(d_ff_3_q));
  D_Flip_Flop d_ff_4 (.D(d_ff_3_q), .clk(clock_1_out), .Q(d_ff_4_q));  // open: Qn, preset, reset
  LED led_4 (.in(d_ff_4_q));

  // Notes on the sheet:
  //   Serial input
  //   SIPO
  //   Q3
  //   Q2
  //   Q1
  //   Q0
endmodule
