// Logisim project SISO_LEFT_SHIFT_OPERATION.circ as structural Verilog: 1 circuit, main circuit main
module main (
  input  in_1,
  input  in_2
);

  wire clock_1_out, d_ff_2_q, d_ff_3_q, d_ff_4_q;

  Clock clock_1 (.out(clock_1_out));
  D_Flip_Flop d_ff_1 (.D(d_ff_2_q), .clk(clock_1_out), .Q(in_1));  // open: Qn, preset, reset
  D_Flip_Flop d_ff_2 (.D(d_ff_3_q), .clk(clock_1_out), .Q(d_ff_2_q));  // open: Qn, preset, reset
  D_Flip_Flop d_ff_3 (.D(d_ff_4_q), .clk(clock_1_out), .Q(d_ff_3_q));  // open: Qn, preset, reset
  D_Flip_Flop d_ff_4 (.D(in_2), .clk(clock_1_out), .Q(d_ff_4_q));  // open: Qn, preset, reset

  // Notes on the sheet:
  //   SISO LEFT SHIFT
  //   Serial output
  //   SERIAL INPUT
endmodule
