// Logisim project SYNCHRONOUS_MOD_6_COUNTER.circ as structural Verilog: 1 circuit, main circuit main
module main (
);

  wire and_1_out, clock_1_out, j_k_ff_1_q, j_k_ff_1_qn, j_k_ff_2_q, j_k_ff_2_qn, j_k_ff_3_q, j_k_ff_3_qn;

  Clock clock_1 (.out(clock_1_out));
  and and_1 (and_1_out, j_k_ff_2_q, j_k_ff_3_q);
  J_K_Flip_Flop j_k_ff_1 (
    .J(and_1_out), .K(j_k_ff_2_qn), .clk(clock_1_out), .Q(j_k_ff_1_q), .Qn(j_k_ff_1_qn));  // open: preset, reset
  LED led_1 (.in(j_k_ff_1_q));
  LED led_2 (.in(j_k_ff_2_q));
  J_K_Flip_Flop j_k_ff_2 (
    .J(j_k_ff_3_qn), .K(j_k_ff_1_q), .clk(clock_1_out), .Q(j_k_ff_2_q), .Qn(j_k_ff_2_qn));  // open: preset, reset
  J_K_Flip_Flop j_k_ff_3 (
    .J(j_k_ff_2_q), .K(j_k_ff_1_qn), .clk(clock_1_out), .Q(j_k_ff_3_q), .Qn(j_k_ff_3_qn));  // open: preset, reset
  LED led_3 (.in(j_k_ff_3_q));

  // Notes on the sheet:
  //   SYNCHRONOUS MOD 6 COUNTER 
endmodule
