// Logisim project mod_8_aysnchronous_counter.circ as structural Verilog: 1 circuit, main circuit main
module main (
  input  in_1
);

  wire clock_1_out, t_ff_1_q, t_ff_1_qn, t_ff_2_q, t_ff_2_qn, t_ff_3_q;

  T_Flip_Flop t_ff_1 (.T(in_1), .clk(clock_1_out), .Q(t_ff_1_q), .Qn(t_ff_1_qn));  // open: reset, preset
  Clock clock_1 (.out(clock_1_out));
  T_Flip_Flop t_ff_2 (.T(in_1), .clk(t_ff_1_qn), .Q(t_ff_2_q), .Qn(t_ff_2_qn));  // open: reset, preset
  T_Flip_Flop t_ff_3 (.T(in_1), .clk(t_ff_2_qn), .Q(t_ff_3_q));  // open: Qn, reset, preset
  LED led_1 (.in(t_ff_1_q));
  LED led_2 (.in(t_ff_2_q));
  LED led_3 (.in(t_ff_3_q));

  // Notes on the sheet:
  //   MOD 8 ASYNCHRONOUS COUNTER 
endmodule
